// Logisim project cpu.circ as structural Verilog: 1 circuit, main circuit main
module main (
  input  reg_rst
);

  wire clk_out, decoder_1_out0, decoder_1_out1, decoder_1_out2, decoder_1_out3, decoder_1_out4,
       decoder_1_out5, decoder_1_out6, decoder_1_out7, decoder_1_out8, decoder_1_out9, decoder_1_out10,
       decoder_1_out11, decoder_1_out12, decoder_1_out13, decoder_1_out14, decoder_1_out15, decoder_2_out0,
       decoder_2_out1, decoder_2_out2, decoder_2_out3, decoder_2_out4, decoder_2_out5, decoder_2_out6,
       decoder_2_out7, decoder_2_out8, decoder_2_out9, decoder_2_out10, decoder_2_out11, decoder_2_out12,
       decoder_2_out13, decoder_2_out14, decoder_2_out15, decoder_3_out0, decoder_3_out1, decoder_3_out2,
       decoder_3_out3, decoder_3_out4, decoder_3_out5, decoder_3_out6, decoder_3_out7, decoder_3_out8,
       decoder_3_out9, decoder_3_out10, decoder_3_out11, decoder_3_out12, decoder_3_out13, decoder_3_out14,
       decoder_3_out15;
  wire [3:0] rd_sel_sw4, rs_sel_sw4, rt_sel_sw4;
  wire [15:0] controlled_buffer_1_out, controlled_buffer_2_out, controlled_buffer_3_out,
       controlled_buffer_4_out, controlled_buffer_5_out, controlled_buffer_6_out, controlled_buffer_7_out,
       controlled_buffer_8_out, controlled_buffer_9_out, controlled_buffer_10_out, controlled_buffer_11_out,
       controlled_buffer_12_out, controlled_buffer_13_out, controlled_buffer_14_out,
       controlled_buffer_15_out, controlled_buffer_16_out, controlled_buffer_17_out,
       controlled_buffer_18_out, controlled_buffer_19_out, controlled_buffer_20_out,
       controlled_buffer_21_out, controlled_buffer_22_out, controlled_buffer_23_out,
       controlled_buffer_24_out, controlled_buffer_25_out, controlled_buffer_26_out,
       controlled_buffer_27_out, controlled_buffer_28_out, controlled_buffer_29_out,
       controlled_buffer_30_out, controlled_buffer_31_out, controlled_buffer_32_out, R0_q, R1_q, R2_q, R3_q,
       R4_q, R5_q, R6_q, R7_q, R8_q, R9_q, R10_q, R11_q, R12_q, R13_q, R14_q, R15_q, undriven, undriven_2,
       undriven_3, undriven_4, undriven_5, undriven_6, undriven_7, undriven_8, undriven_9, undriven_10,
       undriven_11, undriven_12, undriven_13, undriven_14, undriven_15, undriven_16;

  DipSwitch #(.number(4)) rd_sel (.sw1(rd_sel_sw4[3]), .sw2(rd_sel_sw4[2]), .sw3(rd_sel_sw4[1]), .sw4(rd_sel_sw4[0]));
  DipSwitch #(.number(4)) rs_sel (.sw1(rs_sel_sw4[3]), .sw2(rs_sel_sw4[2]), .sw3(rs_sel_sw4[1]), .sw4(rs_sel_sw4[0]));
  DipSwitch #(.number(4)) rt_sel (.sw1(rt_sel_sw4[3]), .sw2(rt_sel_sw4[2]), .sw3(rt_sel_sw4[1]), .sw4(rt_sel_sw4[0]));
  Decoder #(.enable("false"), .select(4)) decoder_1 (
    .out0(decoder_1_out0), .out1(decoder_1_out1), .out2(decoder_1_out2), .out3(decoder_1_out3),
    .out4(decoder_1_out4), .out5(decoder_1_out5), .out6(decoder_1_out6), .out7(decoder_1_out7),
    .out8(decoder_1_out8), .out9(decoder_1_out9), .out10(decoder_1_out10), .out11(decoder_1_out11),
    .out12(decoder_1_out12), .out13(decoder_1_out13), .out14(decoder_1_out14), .out15(decoder_1_out15),
    .sel(rd_sel_sw4));
  Decoder #(.enable("false"), .select(4)) decoder_2 (
    .out0(decoder_2_out0), .out1(decoder_2_out1), .out2(decoder_2_out2), .out3(decoder_2_out3),
    .out4(decoder_2_out4), .out5(decoder_2_out5), .out6(decoder_2_out6), .out7(decoder_2_out7),
    .out8(decoder_2_out8), .out9(decoder_2_out9), .out10(decoder_2_out10), .out11(decoder_2_out11),
    .out12(decoder_2_out12), .out13(decoder_2_out13), .out14(decoder_2_out14), .out15(decoder_2_out15),
    .sel(rs_sel_sw4));
  Decoder #(.enable("false"), .select(4)) decoder_3 (
    .out0(decoder_3_out0), .out1(decoder_3_out1), .out2(decoder_3_out2), .out3(decoder_3_out3),
    .out4(decoder_3_out4), .out5(decoder_3_out5), .out6(decoder_3_out6), .out7(decoder_3_out7),
    .out8(decoder_3_out8), .out9(decoder_3_out9), .out10(decoder_3_out10), .out11(decoder_3_out11),
    .out12(decoder_3_out12), .out13(decoder_3_out13), .out14(decoder_3_out14), .out15(decoder_3_out15),
    .sel(rt_sel_sw4));
  Clock clk (.out(clk_out));
  Register #(.width(16)) R7 (.D(undriven_2), .en(decoder_1_out7), .clk(clk_out), .Q(R7_q), .clr(reg_rst));
  assign controlled_buffer_1_out = decoder_2_out15 ? R15_q : 16'bz;  // Controlled_Buffer controlled_buffer_1
  Register #(.width(16)) R15 (.D(undriven), .en(decoder_1_out15), .clk(clk_out), .Q(R15_q), .clr(reg_rst));
  assign controlled_buffer_2_out = decoder_2_out7 ? R7_q : 16'bz;  // Controlled_Buffer controlled_buffer_2
  assign controlled_buffer_3_out = decoder_3_out15 ? R15_q : 16'bz;  // Controlled_Buffer controlled_buffer_3
  assign controlled_buffer_4_out = decoder_3_out7 ? R7_q : 16'bz;  // Controlled_Buffer controlled_buffer_4
  Register #(.width(16)) R6 (.D(undriven_4), .en(decoder_1_out6), .clk(clk_out), .Q(R6_q), .clr(reg_rst));
  assign controlled_buffer_5_out = decoder_2_out14 ? R14_q : 16'bz;  // Controlled_Buffer controlled_buffer_5
  Register #(.width(16)) R14 (.D(undriven_3), .en(decoder_1_out14), .clk(clk_out), .Q(R14_q), .clr(reg_rst));
  assign controlled_buffer_6_out = decoder_2_out6 ? R6_q : 16'bz;  // Controlled_Buffer controlled_buffer_6
  assign controlled_buffer_7_out = decoder_3_out14 ? R14_q : 16'bz;  // Controlled_Buffer controlled_buffer_7
  assign controlled_buffer_8_out = decoder_3_out6 ? R6_q : 16'bz;  // Controlled_Buffer controlled_buffer_8
  Register #(.width(16)) R5 (.D(undriven_6), .en(decoder_1_out5), .clk(clk_out), .Q(R5_q), .clr(reg_rst));
  assign controlled_buffer_9_out = decoder_2_out13 ? R13_q : 16'bz;  // Controlled_Buffer controlled_buffer_9
  Register #(.width(16)) R13 (.D(undriven_5), .en(decoder_1_out13), .clk(clk_out), .Q(R13_q), .clr(reg_rst));
  assign controlled_buffer_10_out = decoder_2_out5 ? R5_q : 16'bz;  // Controlled_Buffer controlled_buffer_10
  assign controlled_buffer_11_out = decoder_3_out13 ? R13_q : 16'bz;  // Controlled_Buffer controlled_buffer_11
  assign controlled_buffer_12_out = decoder_3_out5 ? R5_q : 16'bz;  // Controlled_Buffer controlled_buffer_12
  Register #(.width(16)) R4 (.D(undriven_8), .en(decoder_1_out4), .clk(clk_out), .Q(R4_q), .clr(reg_rst));
  assign controlled_buffer_13_out = decoder_2_out12 ? R12_q : 16'bz;  // Controlled_Buffer controlled_buffer_13
  Register #(.width(16)) R12 (.D(undriven_7), .en(decoder_1_out12), .clk(clk_out), .Q(R12_q), .clr(reg_rst));
  assign controlled_buffer_14_out = decoder_2_out4 ? R4_q : 16'bz;  // Controlled_Buffer controlled_buffer_14
  assign controlled_buffer_15_out = decoder_3_out12 ? R12_q : 16'bz;  // Controlled_Buffer controlled_buffer_15
  assign controlled_buffer_16_out = decoder_3_out4 ? R4_q : 16'bz;  // Controlled_Buffer controlled_buffer_16
  Register #(.width(16)) R3 (.D(undriven_10), .en(decoder_1_out3), .clk(clk_out), .Q(R3_q), .clr(reg_rst));
  assign controlled_buffer_17_out = decoder_2_out11 ? R11_q : 16'bz;  // Controlled_Buffer controlled_buffer_17
  Register #(.width(16)) R11 (.D(undriven_9), .en(decoder_1_out11), .clk(clk_out), .Q(R11_q), .clr(reg_rst));
  assign controlled_buffer_18_out = decoder_2_out3 ? R3_q : 16'bz;  // Controlled_Buffer controlled_buffer_18
  assign controlled_buffer_19_out = decoder_3_out11 ? R11_q : 16'bz;  // Controlled_Buffer controlled_buffer_19
  assign controlled_buffer_20_out = decoder_3_out3 ? R3_q : 16'bz;  // Controlled_Buffer controlled_buffer_20
  Register #(.width(16)) R2 (.D(undriven_12), .en(decoder_1_out2), .clk(clk_out), .Q(R2_q), .clr(reg_rst));
  assign controlled_buffer_21_out = decoder_2_out10 ? R10_q : 16'bz;  // Controlled_Buffer controlled_buffer_21
  Register #(.width(16)) R10 (.D(undriven_11), .en(decoder_1_out10), .clk(clk_out), .Q(R10_q), .clr(reg_rst));
  assign controlled_buffer_22_out = decoder_2_out2 ? R2_q : 16'bz;  // Controlled_Buffer controlled_buffer_22
  assign controlled_buffer_23_out = decoder_3_out10 ? R10_q : 16'bz;  // Controlled_Buffer controlled_buffer_23
  assign controlled_buffer_24_out = decoder_3_out2 ? R2_q : 16'bz;  // Controlled_Buffer controlled_buffer_24
  Register #(.width(16)) R1 (.D(undriven_14), .en(decoder_1_out1), .clk(clk_out), .Q(R1_q), .clr(reg_rst));
  assign controlled_buffer_25_out = decoder_2_out9 ? R9_q : 16'bz;  // Controlled_Buffer controlled_buffer_25
  Register #(.width(16)) R9 (.D(undriven_13), .en(decoder_1_out9), .clk(clk_out), .Q(R9_q), .clr(reg_rst));
  assign controlled_buffer_26_out = decoder_2_out1 ? R1_q : 16'bz;  // Controlled_Buffer controlled_buffer_26
  assign controlled_buffer_27_out = decoder_3_out9 ? R9_q : 16'bz;  // Controlled_Buffer controlled_buffer_27
  assign controlled_buffer_28_out = decoder_3_out1 ? R1_q : 16'bz;  // Controlled_Buffer controlled_buffer_28
  Register #(.width(16)) R0 (.D(undriven_16), .en(decoder_1_out0), .clk(clk_out), .Q(R0_q), .clr(reg_rst));
  assign controlled_buffer_29_out = decoder_2_out8 ? R8_q : 16'bz;  // Controlled_Buffer controlled_buffer_29
  Register #(.width(16)) R8 (.D(undriven_15), .en(decoder_1_out8), .clk(clk_out), .Q(R8_q), .clr(reg_rst));
  assign controlled_buffer_30_out = decoder_2_out0 ? R0_q : 16'bz;  // Controlled_Buffer controlled_buffer_30
  assign controlled_buffer_31_out = decoder_3_out8 ? R8_q : 16'bz;  // Controlled_Buffer controlled_buffer_31
  assign controlled_buffer_32_out = decoder_3_out0 ? R0_q : 16'bz;  // Controlled_Buffer controlled_buffer_32

  // Notes on the sheet:
  //   Rd Selector
endmodule
